// Digital circuit CPU.dig as structural Verilog
module CPU (
  input  clk
);

  wire button_1_out, Clk_t, counter_1_ovf, dipswitch_2_out, not_1_out, or_1_out, ROM_Out;
  wire [3:0] Boot_d, Boot_d_2, Boot_d_3, Boot_d_4, Boot_d_5, Boot_d_6, Boot_d_7, Boot_d_8, counter_1_out,
       counter_1_out_2, counter_1_out_3, counter_1_out_4, counter_1_out_5;
  wire [23:20] counter_1_out_6;

  DipSwitch dipswitch_1 (.out(ROM_Out));
  Button button_1 (.out(button_1_out));
  DipSwitch dipswitch_2 (.out(dipswitch_2_out));
  not not_1 (not_1_out, or_1_out);
  Multiplexer multiplexer_1 (.sel(dipswitch_2_out), .in_0(button_1_out), .in_1(clk), .out(Clk_t));
  or or_1 (or_1_out, or_1_out, counter_1_ovf);
  Counter #(.Bits(24)) counter_1 (
    .en(not_1_out), .C(Clk_t), .clr(1'b0),
    .out({counter_1_out_6, counter_1_out_5, counter_1_out_4, counter_1_out_3, counter_1_out_2, counter_1_out}),
    .ovf(counter_1_ovf));
  ROM #(.AddrBits(24), .Bits(32)) Boot (
    .A({counter_1_out_6, counter_1_out_5, counter_1_out_4, counter_1_out_3, counter_1_out_2, counter_1_out}),
    .sel(ROM_Out), .D({Boot_d_8, Boot_d_7, Boot_d_6, Boot_d_5, Boot_d_4, Boot_d_3, Boot_d_2, Boot_d}));
  Seven_Seg_Hex seven_seg_hex_1 (.d(counter_1_out_6), .dp(1'b0));
  Seven_Seg_Hex seven_seg_hex_2 (.d(counter_1_out_5), .dp(1'b0));
  Seven_Seg_Hex seven_seg_hex_3 (.d(counter_1_out_4), .dp(1'b0));
  Seven_Seg_Hex seven_seg_hex_4 (.d(Boot_d_8), .dp(1'b0));
  Seven_Seg_Hex seven_seg_hex_5 (.d(counter_1_out_3), .dp(1'b0));
  Seven_Seg_Hex seven_seg_hex_6 (.d(Boot_d_7), .dp(1'b0));
  Seven_Seg_Hex seven_seg_hex_7 (.d(counter_1_out_2), .dp(1'b0));
  Seven_Seg_Hex seven_seg_hex_8 (.d(Boot_d_6), .dp(1'b0));
  Seven_Seg_Hex seven_seg_hex_9 (.d(counter_1_out), .dp(1'b0));
  Seven_Seg_Hex seven_seg_hex_10 (.d(Boot_d_5), .dp(1'b0));
  Seven_Seg_Hex seven_seg_hex_11 (.d(Boot_d_4), .dp(1'b0));
  Seven_Seg_Hex seven_seg_hex_12 (.d(Boot_d_3), .dp(1'b0));
  Seven_Seg_Hex seven_seg_hex_13 (.d(Boot_d_2), .dp(1'b0));
  Seven_Seg_Hex seven_seg_hex_14 (.d(Boot_d), .dp(1'b0));

  // Notes on the sheet:
  //   clk: Hz: 500
  //   Boot loads boot.pyc
endmodule
