// Digital circuit CPU.dig as structural Verilog
module CPU (
  input  clk,
  input  clk_2,
  input  [31:0] Interface
);

  wire and_4_out, and_5_out, and_6_out, BootSeq_Active, button_1_out, button_2_out, button_3_out,
       button_4_out, button_5_out, Clk_t, Clk_t_t, comparator_1_eq, Ctrl_Alloc, Ctrl_AllocOut, Ctrl_BusMux0,
       Ctrl_BusMux1, Ctrl_Dealloc, Ctrl_ExecEn, Ctrl_ExecInst, Ctrl_Halt, Ctrl_InterfaceOut, Ctrl_LoadInst,
       Ctrl_MemAddrIn, Ctrl_MemDataIn, Ctrl_MemDataOut, Ctrl_PC_Out, Ctrl_PCIn, Ctrl_PCInc,
       Ctrl_SetFirstBlock, dipswitch_1_out, dipswitch_2_out, Halt, Hold, mmu_1_p10, mmu_1_p11, mmu_1_p12,
       multiplexer_1_out, multiplexer_3_out, multiplexer_6_out, multiplexer_7_out, not_2_out, not_3_out,
       not_5_out, not_6_out, not_7_out, not_8_out, or_2_out, or_3_out, or_4_out, or_5_out, or_6_out,
       or_7_out, or_8_out, or_9_out, or_10_out, or_11_out, or_12_out, or_13_out, or_14_out, rs_ff_as_2_q,
       rs_ff_as_3_q, ShadCp_Active, ShadCp_Activen, ShadCpClk, State_Set;
  wire [0:0] undriven;
  wire [3:0] Step_out;
  wire [7:0] Instruction_q, multiplexer_8_out, Parameter_q, State, State_q, Validator_d;
  wire [17:12] driver_6_out;
  wire [31:0] Address, Boot_Sequencer_d, Bus, Bus_Unmuxed, Bytecode_Executor_d, MemAddrIn_out, MemoryAddr_q,
       mmu_1_p7, mmu_1_p8, multiplexer_5_out, Program_Counter_out, ShadCp_Addr;

  PullDown #(.Bits(32)) pulldown_1 (.out(Bus_Unmuxed));
  Multiplexer multiplexer_1 (.sel(dipswitch_1_out), .in_0(clk), .in_1(button_1_out), .out(multiplexer_1_out));
  Button button_1 (.out(button_1_out));
  DipSwitch dipswitch_1 (.out(dipswitch_1_out));
  and and_1 (ShadCpClk, ShadCp_Active, multiplexer_1_out);
  not not_1 (ShadCp_Active, ShadCp_Activen);
  Counter #(.Bits(32)) counter_1 (.en(ShadCp_Active), .C(ShadCpClk), .clr(1'b0), .out(ShadCp_Addr));  // open: ovf
  // MMU mmu_1: pin names not known; wires that end beside it: Ctrl_Alloc, Ctrl_Dealloc, Ctrl_AllocOut, Ctrl_SetFirstBlock, Clk_t, Bus, mmu_1_p7, mmu_1_p8, mmu_1_p7, mmu_1_p10, mmu_1_p11, mmu_1_p12
  or or_1 (ShadCp_Activen, ShadCp_Activen, comparator_1_eq);
  Comparator #(.Bits(32)) comparator_1 (.a(ShadCp_Addr), .b(32'h100000), .eq(comparator_1_eq));  // open: gt, lt
  Register #(.Bits(32)) MemoryAddr (.D(Bus), .C(Clk_t), .en(Ctrl_MemAddrIn), .Q(MemoryAddr_q));
  Multiplexer #(.Selector_Bits(2), .Bits(32)) multiplexer_2 (
    .sel({Ctrl_BusMux1, Ctrl_BusMux0}), .in_0(Bus_Unmuxed), .in_1({Bus_Unmuxed[23:0], Bus_Unmuxed[31:24]}),
    .in_2({Bus_Unmuxed[15:0], Bus_Unmuxed[31:16]}), .in_3({Bus_Unmuxed[7:0], Bus_Unmuxed[31:8]}), .out(Bus));
  Multiplexer multiplexer_3 (.sel(mmu_1_p12), .in_0(mmu_1_p10), .in_1(Ctrl_MemDataIn), .out(multiplexer_3_out));
  PullDown #(.Bits(32)) pulldown_2 (.out(Bus));
  Multiplexer #(.Bits(32)) multiplexer_4 (
    .sel(ShadCp_Activen), .in_0(ShadCp_Addr), .in_1(multiplexer_5_out), .out(Address));
  Multiplexer #(.Bits(32)) multiplexer_5 (
    .sel(mmu_1_p12), .in_0(mmu_1_p8), .in_1(MemoryAddr_q), .out(multiplexer_5_out));
  or or_2 (or_2_out, ShadCp_Active, multiplexer_3_out);
  Multiplexer multiplexer_6 (.sel(mmu_1_p12), .in_0(mmu_1_p11), .in_1(Ctrl_MemDataOut), .out(multiplexer_6_out));
  or or_3 (or_3_out, ShadCpClk, Clk_t);
  PullUp pullup_1 (.out(Halt));
  not not_2 (not_2_out, Halt);
  // ROM rom_1: pin names not known; wires that end beside it: Address, ShadCp_Active, mmu_1_p7
  RAM ram_1 (.Addr(Address), .D_In(mmu_1_p7), .Str(or_2_out), .Clk(or_3_out), .Ld(multiplexer_6_out), .D_Out(mmu_1_p7));
  Button button_2 (.out(button_2_out));
  Multiplexer multiplexer_7 (.sel(dipswitch_2_out), .in_0(button_2_out), .in_1(clk_2), .out(multiplexer_7_out));
  DipSwitch dipswitch_2 (.out(dipswitch_2_out));
  or or_4 (or_4_out, not_2_out, or_4_out);
  and and_2 (Hold, ShadCp_Activen, mmu_1_p12);
  and and_3 (Clk_t, multiplexer_7_out, not_3_out);
  not not_3 (not_3_out, or_4_out);
  assign Halt = Ctrl_Halt ? 1'b0 : 1'bz;  // Driver driver_1
  assign Bus_Unmuxed = or_5_out ? mmu_1_p7 : 32'bz;  // Driver driver_2
  assign mmu_1_p7 = Ctrl_MemDataIn ? Bus : 32'bz;  // Driver driver_3
  not not_4 (Clk_t_t, Clk_t);
  or or_5 (or_5_out, Ctrl_MemDataOut, ShadCp_Active);
  ROM #(.bigEndian("true"), .AddrBits(8), .Bits(8)) Validator (.A(Instruction_q), .sel(1'b1), .D(Validator_d));
  and and_4 (and_4_out, State_Set, not_5_out);
  or or_6 (or_6_out, Ctrl_ExecInst, State_Set);
  Multiplexer #(.Bits(8)) multiplexer_8 (.sel(State_Set), .in_0(Instruction_q), .in_1(State), .out(multiplexer_8_out));
  LED led_1 (.in(Validator_d[0]));
  CounterPreset #(.Bits(32), .isProgramCounter("true")) Program_Counter (
    .en(Ctrl_PCInc), .C(Clk_t), .dir(1'b0), .in(Bus), .ld(Ctrl_PCIn), .clr(1'b0), .out(Program_Counter_out));  // open: ovf
  or or_7 (or_7_out, and_4_out, or_8_out);
  or or_8 (or_8_out, Ctrl_ExecEn, Ctrl_ExecInst);
  not not_5 (not_5_out, BootSeq_Active);
  Register #(.Bits(8)) Instruction (.D(Bus[31:24]), .C(Clk_t), .en(Ctrl_LoadInst), .Q(Instruction_q));
  not not_6 (not_6_out, Validator_d[0]);
  Register #(.Bits(8)) Parameter (.D(Bus[23:16]), .C(Clk_t), .en(Ctrl_LoadInst), .Q(Parameter_q));
  // Probe on Program_Counter_out
  assign Bus_Unmuxed = Ctrl_PC_Out ? Program_Counter_out : 32'bz;  // Driver driver_4
  Counter #(.Bits(4)) Step (.en(Hold), .C(Clk_t), .clr(or_7_out), .out(Step_out));  // open: ovf
  Register #(.Bits(8)) u_State (.D(multiplexer_8_out), .C(Clk_t), .en(or_6_out), .Q(State_q));
  assign Halt = not_6_out ? 1'b0 : 1'bz;  // Driver driver_5
  Seven_Seg_Hex seven_seg_hex_1 (.d(State_q[7:4]), .dp(1'b0));
  Seven_Seg_Hex seven_seg_hex_2 (.d(Instruction_q[7:4]), .dp(1'b0));
  Seven_Seg_Hex seven_seg_hex_3 (.d(Parameter_q[7:4]), .dp(1'b0));
  Seven_Seg_Hex seven_seg_hex_4 (.d(Address[31:28]), .dp(1'b0));
  ROM #(.bigEndian("true"), .AddrBits(4), .Bits(32)) Boot_Sequencer (.A(Step_out), .sel(1'b1), .D(Boot_Sequencer_d));
  ROM #(.bigEndian("true"), .AddrBits(16), .Bits(32)) Bytecode_Executor (
    .A({State_q, Step_out, 3'b000, undriven[0]}), .sel(1'b1), .D(Bytecode_Executor_d));
  Seven_Seg_Hex seven_seg_hex_5 (.d(State_q[3:0]), .dp(1'b0));
  Seven_Seg_Hex seven_seg_hex_6 (.d(Instruction_q[3:0]), .dp(1'b0));
  Seven_Seg_Hex seven_seg_hex_7 (.d(Parameter_q[3:0]), .dp(1'b0));
  Seven_Seg_Hex seven_seg_hex_8 (.d(Address[27:24]), .dp(1'b0));
  assign {State, State_Set, Ctrl_Halt, Ctrl_ExecEn, Ctrl_InterfaceOut, Ctrl_BusMux1, Ctrl_BusMux0, driver_6_out, Ctrl_PC_Out, Ctrl_PCIn, Ctrl_PCInc, Ctrl_ExecInst, Ctrl_LoadInst, Ctrl_AllocOut, Ctrl_SetFirstBlock, Ctrl_Dealloc, Ctrl_Alloc, Ctrl_MemDataOut, Ctrl_MemDataIn, Ctrl_MemAddrIn} = BootSeq_Active ? Boot_Sequencer_d : 32'bz;  // Driver driver_6
  assign {State, State_Set, Ctrl_Halt, Ctrl_ExecEn, Ctrl_InterfaceOut, Ctrl_BusMux1, Ctrl_BusMux0, driver_6_out, Ctrl_PC_Out, Ctrl_PCIn, Ctrl_PCInc, Ctrl_ExecInst, Ctrl_LoadInst, Ctrl_AllocOut, Ctrl_SetFirstBlock, Ctrl_Dealloc, Ctrl_Alloc, Ctrl_MemDataOut, Ctrl_MemDataIn, Ctrl_MemAddrIn} = rs_ff_as_2_q ? Bytecode_Executor_d : 32'bz;  // Driver driver_7
  PullDown #(.Bits(32)) pulldown_3 (.out({State, State_Set, Ctrl_Halt, Ctrl_ExecEn, Ctrl_InterfaceOut, Ctrl_BusMux1, Ctrl_BusMux0, driver_6_out, Ctrl_PC_Out, Ctrl_PCIn, Ctrl_PCInc, Ctrl_ExecInst, Ctrl_LoadInst, Ctrl_AllocOut, Ctrl_SetFirstBlock, Ctrl_Dealloc, Ctrl_Alloc, Ctrl_MemDataOut, Ctrl_MemDataIn, Ctrl_MemAddrIn}));
  Seven_Seg_Hex seven_seg_hex_9 (.d(Address[23:20]), .dp(1'b0));
  Seven_Seg_Hex seven_seg_hex_10 (.d(Address[19:16]), .dp(1'b0));
  LED led_2 (.in(BootSeq_Active));
  LED led_3 (.in(rs_ff_as_2_q));
  LED led_4 (.in(rs_ff_as_3_q));
  or or_9 (or_9_out, BootSeq_Active, rs_ff_as_2_q, rs_ff_as_3_q);
  Seven_Seg_Hex seven_seg_hex_11 (.d(Address[15:12]), .dp(1'b0));
  RS_FF_AS rs_ff_as_1 (.S(or_13_out), .R(or_10_out), .Q(BootSeq_Active));  // open: nQ
  RS_FF_AS rs_ff_as_2 (.S(or_14_out), .R(or_11_out), .Q(rs_ff_as_2_q));  // open: nQ
  RS_FF_AS rs_ff_as_3 (.S(button_5_out), .R(or_12_out), .Q(rs_ff_as_3_q));  // open: nQ
  not not_7 (not_7_out, or_9_out);
  not not_8 (not_8_out, rs_ff_as_2_q);
  Seven_Seg_Hex seven_seg_hex_12 (.d(Address[11:8]), .dp(1'b0));
  or or_10 (or_10_out, button_5_out, or_14_out);
  or or_11 (or_11_out, button_5_out, or_13_out);
  or or_12 (or_12_out, or_14_out, or_13_out);
  and and_5 (and_5_out, ShadCp_Activen, not_7_out);
  Seven_Seg_Hex seven_seg_hex_13 (.d(Address[7:4]), .dp(1'b0));
  and and_6 (and_6_out, not_8_out, Ctrl_ExecEn);
  Seven_Seg_Hex seven_seg_hex_14 (.d(Address[3:0]), .dp(1'b0));
  Button button_3 (.out(button_3_out));
  or or_13 (or_13_out, and_5_out, button_3_out);
  Button button_4 (.out(button_4_out));
  or or_14 (or_14_out, and_6_out, button_4_out);
  Button button_5 (.out(button_5_out));
  Seven_Seg_Hex seven_seg_hex_15 (.d(Bus[31:28]), .dp(1'b0));
  DipSwitch MemAddrIn (.out(MemAddrIn_out[0]));
  DipSwitch MemDataIn (.out(MemAddrIn_out[1]));
  DipSwitch MemDataOut (.out(MemAddrIn_out[2]));
  DipSwitch Alloc (.out(MemAddrIn_out[3]));
  DipSwitch Dealloc (.out(MemAddrIn_out[4]));
  DipSwitch SetFirstBlock (.out(MemAddrIn_out[5]));
  DipSwitch AllocOut (.out(MemAddrIn_out[6]));
  DipSwitch LoadInstr (.out(MemAddrIn_out[7]));
  DipSwitch ExecInstr (.out(MemAddrIn_out[8]));
  DipSwitch PCInc (.out(MemAddrIn_out[9]));
  DipSwitch PCIn (.out(MemAddrIn_out[10]));
  DipSwitch PCOut (.out(MemAddrIn_out[11]));
  DipSwitch dipswitch_3 (.out(MemAddrIn_out[12]));
  DipSwitch dipswitch_4 (.out(MemAddrIn_out[13]));
  DipSwitch dipswitch_5 (.out(MemAddrIn_out[14]));
  DipSwitch dipswitch_6 (.out(MemAddrIn_out[15]));
  DipSwitch dipswitch_7 (.out(MemAddrIn_out[16]));
  DipSwitch dipswitch_8 (.out(MemAddrIn_out[17]));
  DipSwitch BusMux0 (.out(MemAddrIn_out[18]));
  DipSwitch BusMux1 (.out(MemAddrIn_out[19]));
  DipSwitch InterfaceOut (.out(MemAddrIn_out[20]));
  DipSwitch ExecEn (.out(MemAddrIn_out[21]));
  DipSwitch u_Halt (.out(MemAddrIn_out[22]));
  DipSwitch u_State_Set (.out(MemAddrIn_out[23]));
  DipSwitch State_0 (.out(MemAddrIn_out[24]));
  DipSwitch State_1 (.out(MemAddrIn_out[25]));
  DipSwitch State_2 (.out(MemAddrIn_out[26]));
  DipSwitch State_3 (.out(MemAddrIn_out[27]));
  DipSwitch State_4 (.out(MemAddrIn_out[28]));
  DipSwitch State_5 (.out(MemAddrIn_out[29]));
  DipSwitch State_6 (.out(MemAddrIn_out[30]));
  DipSwitch State_7 (.out(MemAddrIn_out[31]));
  Seven_Seg_Hex seven_seg_hex_16 (.d(Bus[27:24]), .dp(1'b0));
  assign {State, State_Set, Ctrl_Halt, Ctrl_ExecEn, Ctrl_InterfaceOut, Ctrl_BusMux1, Ctrl_BusMux0, driver_6_out, Ctrl_PC_Out, Ctrl_PCIn, Ctrl_PCInc, Ctrl_ExecInst, Ctrl_LoadInst, Ctrl_AllocOut, Ctrl_SetFirstBlock, Ctrl_Dealloc, Ctrl_Alloc, Ctrl_MemDataOut, Ctrl_MemDataIn, Ctrl_MemAddrIn} = rs_ff_as_3_q ? MemAddrIn_out : 32'bz;  // Driver driver_8
  Seven_Seg_Hex seven_seg_hex_17 (.d(Bus[23:20]), .dp(1'b0));
  Seven_Seg_Hex seven_seg_hex_18 (.d(Bus[19:16]), .dp(1'b0));
  Seven_Seg_Hex seven_seg_hex_19 (.d(Bus[15:12]), .dp(1'b0));
  Seven_Seg_Hex seven_seg_hex_20 (.d(Bus[11:8]), .dp(1'b0));
  Seven_Seg_Hex seven_seg_hex_21 (.d(Bus[7:4]), .dp(1'b0));
  Seven_Seg_Hex seven_seg_hex_22 (.d(Bus[3:0]), .dp(1'b0));
  assign Bus_Unmuxed = Ctrl_InterfaceOut ? Interface : 32'bz;  // Driver driver_9

  // Notes on the sheet:
  //   clk: Hz: 2147483647
  //   clk_2: Hz: 500000
  //   Bus Muxer
  //   Memory
  //   ABCD
  //   BCDA
  //   CDAB
  //   DABC
  //   Clock
  //   Control
  //   Validator loads validInstructions.bin
  //   Memory Address
  //   Boot_Sequencer loads ucodeBootSeq.bin
  //   Bytecode_Executor loads ucodeByteCodeExec.bin
  //   State
  //   Instruction
  //   Parameter
  //   Bus
endmodule
