// Digital circuit MMU.dig as structural Verilog
module MMU (
  input  Alloc,
  input  DeAlloc,
  input  YieldResult,
  input  SetFirst,
  input  Clk,
  input  [31:0] Bus,
  output [31:0] MemAddr,
  output [31:0] MemData,
  output MemStr,
  output MemLd,
  output CPU_Enable
);

  wire and_1_out, comparator_1_eq, comparator_1_gt, nor_1_out, or_1_out, or_2_out, or_3_out, Step_ovf,
       sub_1_c_o;
  wire [8:1] or_4_out;
  wire [23:0] Microcode_d;
  wire [31:0] add_1_s, Available_q, Desired_q, First_q, Next_q, Previous_q, pulldown_1_out, Split_s, sub_1_s,
       Testing_q;

  Register #(.Bits(3)) State (.D(Microcode_d[2:0]), .C(Clk), .en(Microcode_d[3]), .Q(or_4_out[8:6]));
  Counter #(.Bits(3)) Step (.en(1'b1), .C(Clk), .clr(or_1_out), .out(or_4_out[5:3]), .ovf(Step_ovf));
  or or_1 (or_1_out, Microcode_d[3], Step_ovf);
  // Probe on or_4_out[5:3]
  nor nor_1 (nor_1_out, Alloc, DeAlloc, YieldResult);
  // Probe on or_4_out[8:6]
  ROM #(.bigEndian("true"), .AddrBits(9), .Bits(24)) Microcode (
    .A({or_4_out, Alloc}), .sel(1'b1), .D({Microcode_d[23:8], MemLd, MemStr, CPU_Enable, Microcode_d[4:0]}));
  // Probe on {Microcode_d[23:8], MemLd, MemStr, CPU_Enable, Microcode_d[4:0]}
  and and_1 (and_1_out, SetFirst, nor_1_out);
  PullDown #(.Bits(32)) pulldown_1 (.out(pulldown_1_out));
  assign pulldown_1_out = and_1_out ? Bus : 32'bz;  // Driver driver_1
  Register #(.Bits(32)) Available (.D(pulldown_1_out), .C(Clk), .en(Microcode_d[23]), .Q(Available_q));
  assign pulldown_1_out = Microcode_d[22] ? Available_q : 32'bz;  // Driver driver_2
  Register #(.Bits(32)) Desired (.D(Bus), .C(Clk), .en(Microcode_d[21]), .Q(Desired_q));
  assign pulldown_1_out = Microcode_d[20] ? Desired_q : 32'bz;  // Driver driver_3
  assign pulldown_1_out = MemLd ? MemData : 32'bz;  // Driver driver_4
  assign MemData = MemStr ? pulldown_1_out : 32'bz;  // Driver driver_5
  // Probe on Available_q
  Comparator #(.Bits(32)) comparator_1 (
    .a(Available_q), .b(Desired_q), .gt(comparator_1_gt), .eq(comparator_1_eq));  // open: lt
  Sub #(.Bits(32)) sub_1 (.a(Available_q), .b(Desired_q), .c_i(1'b0), .s(sub_1_s), .c_o(sub_1_c_o));
  // Probe on Desired_q
  or or_2 (or_2_out, and_1_out, Microcode_d[18]);
  Add #(.Bits(32)) add_1 (.a(pulldown_1_out), .b({{31{1'b0}}, Microcode_d[8]}), .c_i(1'b0), .s(add_1_s));  // open: c_o
  or or_3 (or_3_out, Microcode_d[9], Microcode_d[8]);
  or or_4 (or_4_out[2], comparator_1_gt, comparator_1_eq);
  // Probe on add_1_s
  Register #(.Bits(32)) register_1 (.D(add_1_s), .C(Clk), .en(or_3_out), .Q(MemAddr));
  // Probe on sub_1_s
  assign pulldown_1_out = Microcode_d[19] ? sub_1_s : 32'bz;  // Driver driver_6
  Register #(.Bits(32)) First (.D(pulldown_1_out), .C(Clk), .en(or_2_out), .Q(First_q));
  assign pulldown_1_out = Microcode_d[17] ? First_q : 32'bz;  // Driver driver_7
  Register #(.Bits(32)) Previous (.D(pulldown_1_out), .C(Clk), .en(Microcode_d[16]), .Q(Previous_q));
  assign pulldown_1_out = Microcode_d[15] ? Previous_q : 32'bz;  // Driver driver_8
  Register #(.Bits(32)) Testing (.D(pulldown_1_out), .C(Clk), .en(Microcode_d[14]), .Q(Testing_q));
  assign pulldown_1_out = Microcode_d[13] ? Testing_q : 32'bz;  // Driver driver_9
  assign pulldown_1_out = Microcode_d[12] ? Split_s : 32'bz;  // Driver driver_10
  Register #(.Bits(32)) Next (.D(pulldown_1_out), .C(Clk), .en(Microcode_d[11]), .Q(Next_q));
  assign pulldown_1_out = Microcode_d[10] ? Next_q : 32'bz;  // Driver driver_11
  // Probe on First_q
  Comparator #(.Bits(32)) comparator_2 (.a(First_q), .b(Previous_q), .eq(or_4_out[1]));  // open: gt, lt
  // Probe on Previous_q
  // Probe on Testing_q
  // Probe on Next_q
  Add #(.Bits(32)) Split (.a(Testing_q), .b(Desired_q), .c_i(1'b0), .s(Split_s));  // open: c_o
  // Probe on Split_s

  // Notes on the sheet:
  //   CPU_Enable: Pulled low to suspend bytecode execution during allocation and deallocation operations
  //   Microcode loads ucodeMMU.bin
  //   Sufficient
  //   Remaining
  //   PreviousIsFirst
endmodule
