// Digital circuit RAM.dig as structural Verilog
module RAM (
  input  [31:0] Addr,
  input  [31:0] D_In,
  input  Str,
  input  Clk,
  input  Ld,
  output [31:0] D_Out
);

  RAMDualPort #(.AddrBits(24), .Bits(32)) ramdualport_1 (
    .A(Addr[23:0]), .Din(D_In), .str(Str), .C(Clk), .ld(Ld), .D(D_Out));
endmodule
